// Logisim project ALU.circ as structural Verilog: 1 circuit, main circuit main
module main (
);

  wire and_1_out, C_A, C_N, C_S, comparator_1_gt, comparator_2_gt, comparator_3_eq, comparator_3_lt,
       multiplexer_4_out, xnor_1_out, xor_1_out;
  wire [3:0] OPR;
  wire [31:0] ADD, NEG, not_1_out, R, RY, SMIN, SUB, UMIN, X;

  Register #(.width(32)) u_X (.Q(X));  // open: D, en, clk, clr
  Register #(.width(32)) Y (.Q(RY));  // open: D, en, clk, clr
  assign not_1_out = ~RY;  // NOT_Gate not_1, 32 bits wide
  Adder #(.width(32)) adder_1 (.a(X), .b(RY), .out(ADD), .cout(C_A));  // open: cin
  Subtractor #(.width(32)) subtractor_1 (.a(X), .b(RY), .out(SUB), .bout(C_S));  // open: bin
  Adder #(.width(32)) adder_2 (.a(not_1_out), .b(32'h1), .out(NEG), .cout(C_N));  // open: cin
  Multiplexer #(.width(32)) multiplexer_1 (.in0(X), .in1(RY), .out(UMIN), .sel(comparator_1_gt));  // open: en
  Comparator #(.width(32), .mode("unsigned")) comparator_1 (.a(X), .b(RY), .gt(comparator_1_gt));  // open: eq, lt
  Multiplexer #(.width(32)) multiplexer_2 (.in0(X), .in1(RY), .out(SMIN), .sel(comparator_2_gt));  // open: en
  Comparator #(.width(32)) comparator_2 (.a(X), .b(RY), .gt(comparator_2_gt));  // open: eq, lt
  Multiplexer #(.select(4), .width(32)) multiplexer_3 (
    .in0({32{1'b0}}), .in1(ADD), .in2(SUB), .in3(RY), .in9(UMIN), .in10(SMIN), .in14(NEG), .out(R), .sel(OPR));  // open: in4, in5, in6, in7, in8, in11, in12, in13, in15, en
  Register #(.width(4)) register_1 (.Q(OPR));  // open: D, en, clk, clr
  // Probe on R
  // Probe on R
  xnor xnor_1 (xnor_1_out, X[31], RY[31]);
  xor xor_1 (xor_1_out, X[31], R[31]);
  Comparator #(.width(32)) comparator_3 (
    .a(R), .b({32{1'b0}}), .eq(comparator_3_eq), .lt(comparator_3_lt));  // open: gt
  Multiplexer #(.select(4)) multiplexer_4 (
    .in1(C_A), .in2(C_S), .in3(1'b0), .in4(1'b0), .in5(1'b0), .in6(1'b0), .in7(1'b0), .in8(1'b0), .in9(1'b0),
    .in10(1'b0), .in11(1'b0), .in12(1'b0), .in13(1'b0), .in14(C_N), .in15(1'b0), .out(multiplexer_4_out),
    .sel(OPR));  // open: in0, en
  LED C (.in(multiplexer_4_out));
  and and_1 (and_1_out, xnor_1_out, xor_1_out);
  LED V (.in(and_1_out));
  LED Z (.in(comparator_3_eq));
  LED N (.in(comparator_3_lt));

  // Other names for the same wires on the sheet: Y[31:0] = RY
endmodule
