// Logisim project FSM with ROM.circ as structural Verilog: 1 circuit, main circuit main
module main (
);

  wire t_ff_1_q;
  wire [2:0] Current_State_q;
  wire [5:0] rom_1_data;

  T_Flip_Flop #(.trigger("falling")) t_ff_1 (.Q(t_ff_1_q));  // open: clk, T, Qn, preset, reset, en
  Register #(.width(3), .trigger("falling")) Current_State (
    .D(rom_1_data[2:0]), .Q(Current_State_q), .clk(t_ff_1_q));  // open: en, clr
  ROM #(.addrWidth(3), .dataWidth(6)) rom_1 (.addr(Current_State_q), .data(rom_1_data));  // open: sel
  LED O0 (.in(rom_1_data[3]));
  LED O2 (.in(rom_1_data[5]));
  LED O1 (.in(rom_1_data[4]));

  // Notes on the sheet:
  //   contents of rom_1 (hex, n*v repeats v):
  //   4 15 13 8 9 22
endmodule
