// Logisim project ALUOther.circ as structural Verilog: 1 circuit, main circuit main
module main (
);

  wire and_1_out, and_2_out, comparator_1_gt, comparator_2_gt, comparator_3_eq, comparator_3_lt, xnor_1_out,
       xor_1_out;
  wire [3:0] register_1_q;
  wire [31:0] ADD, NEG, R, RY, SMIN, SUB, UMIN, X;

  Register #(.width(32)) u_X (.Q(X));  // open: D, en, clk, clr
  Register #(.width(32)) Y (.Q(RY));  // open: D, en, clk, clr
  Adder #(.width(32)) adder_1 (.a(X), .b(RY), .out(ADD));  // open: cin, cout
  Subtractor #(.width(32)) subtractor_1 (.a(X), .b(X), .out(SUB));  // open: bin, bout
  Negator #(.width(32)) negator_1 (.in(RY), .out(NEG));
  Multiplexer #(.width(32)) multiplexer_1 (.in0(X), .in1(RY), .out(UMIN), .sel(comparator_1_gt));  // open: en
  Comparator #(.width(32), .mode("unsigned")) comparator_1 (.a(X), .b(RY), .gt(comparator_1_gt));  // open: eq, lt
  Multiplexer #(.width(32)) multiplexer_2 (.in0(X), .in1(RY), .out(SMIN), .sel(comparator_2_gt));  // open: en
  Comparator #(.width(32)) comparator_2 (.a(X), .b(RY), .gt(comparator_2_gt));  // open: eq, lt
  Multiplexer #(.select(4), .width(32)) multiplexer_3 (
    .in0({32{1'b0}}), .in1(ADD), .in2(SUB), .in3(RY), .in9(UMIN), .in10(SMIN), .in14(NEG), .out(R),
    .sel(register_1_q));  // open: in4, in5, in6, in7, in8, in11, in12, in13, in15, en
  Register #(.width(4)) register_1 (.Q(register_1_q));  // open: D, en, clk, clr
  // Probe on R
  // Probe on R
  xnor xnor_1 (xnor_1_out, X[31], RY[31]);
  Comparator #(.width(32)) comparator_3 (
    .a(R), .b({32{1'b0}}), .eq(comparator_3_eq), .lt(comparator_3_lt));  // open: gt
  and and_1 (and_1_out, xnor_1_out, RY[31]);
  LED Z (.in(comparator_3_eq));
  LED N (.in(comparator_3_lt));
  LED C (.in(and_2_out));
  and and_2 (and_2_out, X[31], RY[31]);
  xor xor_1 (xor_1_out, and_1_out, R[31]);
  LED V (.in(xor_1_out));

  // Other names for the same wires on the sheet: Y[31:0] = RY
endmodule
