// Logisim project Lab3Part1.circ as structural Verilog: 1 circuit, main circuit main
module main (
);

  wire alu_1_c, alu_1_n, alu_1_v, alu_1_z, CLK, CLR, T1CE, T1OE, T2CE, T2OE, WordR, WordW, xor_1_out;
  wire [1:0] register_1_q;
  wire [3:0] ADDR, OPR;
  wire [15:14] rom_1_data;
  wire [31:0] alu_1_r_32, controlled_buffer_1_out, Data_Bus, T1_dout_32;

  Button button_1 (.out(CLR));
  // Probe on OPR
  T_Flip_Flop Toggle_Switch (.Q(CLK));  // open: clk, T, Qn, preset, reset, en
  LED led_1 (.in(alu_1_z));
  Register #(.width(2)) register_1 (.D(rom_1_data), .Q(register_1_q), .clk(CLK));  // open: en, clr
  Reg32 T1 (.DIn_32(Data_Bus), .CE(T1CE), .DOut_32(T1_dout_32), .CLK(CLK), .OE(T1OE));  // open: Debug_Q_32, Clear
  LED led_2 (.in(alu_1_v));
  LED led_3 (.in(alu_1_n));
  xor xor_1 (xor_1_out, WordR, WordW);
  ALU alu_1 (
    .X_32(T1_dout_32), .Y_32(Data_Bus), .Opr_4(OPR), .R_32(alu_1_r_32), .C(alu_1_c), .V(alu_1_v),
    .N(alu_1_n), .Z(alu_1_z));
  LED led_4 (.in(alu_1_c));
  RAM #(.addrWidth(4), .dataWidth(32)) ram_1 (
    .addr(ADDR), .data(Data_Bus), .sel(xor_1_out), .clk(CLK), .ld(WordR), .clr(CLR));
  ROM #(.addrWidth(2), .dataWidth(16)) rom_1 (
    .addr(register_1_q), .data({rom_1_data, OPR, ADDR, WordR, WordW, T1CE, T1OE, T2CE, T2OE}), .sel(1'b1));
  // Probe on WordW
  // Probe on WordR
  // Probe on T1CE
  // Probe on T1OE
  Reg32 T2 (.DIn_32(alu_1_r_32), .CE(T2CE), .DOut_32(Data_Bus), .CLK(CLK), .OE(T2OE));  // open: Debug_Q_32, Clear
  // Probe on T2CE
  // Probe on T2OE
  assign controlled_buffer_1_out = WordW ? Data_Bus : 32'bz;  // Controlled_Buffer controlled_buffer_1
  // Probe on controlled_buffer_1_out

  // Notes on the sheet:
  //   contents of rom_1 (hex, n*v repeats v):
  //   42e8 8a66 211
endmodule
