// Logisim project Lab3Part2.circ as structural Verilog: 1 circuit, main circuit main
module main (
);

  wire alu_1_c, alu_1_n, alu_1_v, alu_1_z, and_1_out, and_2_out, CLK, CLR, T1CE, T1OE, T2CE, T2OE, WordR,
       WordW, xor_1_out;
  wire [1:0] multiplexer_1_out, register_1_q, rom_1_data_2;
  wire [3:0] ADDR, OPR;
  wire [15:0] register_2_q;
  wire [29:0] rom_1_data;
  wire [31:0] alu_1_r_32, controlled_buffer_1_out, Data_Bus, T1_dout_32;

  Button button_1 (.out(CLR));
  // Probe on OPR
  // Probe on alu_1_r_32
  Reg32 T1 (.DIn_32(Data_Bus), .CE(T1CE), .DOut_32(T1_dout_32), .CLK(CLK), .OE(T1OE));  // open: Debug_Q_32, Clear
  LED led_1 (.in(alu_1_z));
  LED led_2 (.in(alu_1_v));
  LED led_3 (.in(alu_1_n));
  LED led_4 (.in(alu_1_c));
  xor xor_1 (xor_1_out, WordR, WordW);
  ALU alu_1 (
    .X_32(T1_dout_32), .Y_32(Data_Bus), .Opr_4(OPR), .R_32(alu_1_r_32), .C(alu_1_c), .V(alu_1_v),
    .N(alu_1_n), .Z(alu_1_z));
  Reg32 T2 (.DIn_32(alu_1_r_32), .CE(T2CE), .DOut_32(Data_Bus), .CLK(CLK), .OE(T2OE));  // open: Debug_Q_32, Clear
  RAM #(.addrWidth(4), .dataWidth(32)) ram_1 (
    .addr(ADDR), .data(Data_Bus), .sel(xor_1_out), .clk(CLK), .ld(WordR), .clr(CLR));
  assign controlled_buffer_1_out = WordW ? Data_Bus : 32'bz;  // Controlled_Buffer controlled_buffer_1
  // Probe on controlled_buffer_1_out
  T_Flip_Flop Toggle_Switch (.Q(CLK));  // open: clk, T, Qn, preset, reset, en
  Register #(.width(2)) register_1 (.D(multiplexer_1_out), .Q(register_1_q), .clk(CLK));  // open: en, clr
  Multiplexer #(.width(2)) multiplexer_1 (
    .in0(rom_1_data_2), .in1(2'b10), .out(multiplexer_1_out), .sel(and_1_out));  // open: en
  ROM #(.addrWidth(2), .dataWidth(32)) rom_1 (
    .addr(register_1_q),
    .data({rom_1_data_2, rom_1_data[29:25], WordR, WordW, T1CE, T1OE, T2CE, T2OE, rom_1_data[18:0]}));  // open: sel
  and and_1 (and_1_out, ~register_1_q[0], ~register_1_q[1], and_2_out);  // AND_Gate
  and and_2 (and_2_out, register_2_q[12], register_2_q[13], ~register_2_q[15]);  // AND_Gate
  Register #(.width(16)) register_2 (.Q(register_2_q), .clk(CLK));  // open: D, en, clr
  assign OPR = rom_1_data[28] ? 4'b0000 : 4'bz;  // Controlled_Buffer ANOP
  assign OPR = rom_1_data[29] ? register_2_q[15:12] : 4'bz;  // Controlled_Buffer AOP
  assign ADDR = rom_1_data[25] ? register_2_q[3:0] : 4'bz;  // Controlled_Buffer SYR
  assign ADDR = rom_1_data[26] ? register_2_q[7:4] : 4'bz;  // Controlled_Buffer SXR
  assign ADDR = rom_1_data[27] ? register_2_q[11:8] : 4'bz;  // Controlled_Buffer DR
  // Probe on WordR
  // Probe on WordW
  // Probe on T1OE
  // Probe on T1CE
  // Probe on T2OE
  // Probe on T2CE

  // Notes on the sheet:
  //   contents of rom_1 (hex, n*v repeats v):
  //   50000000 95400000 e3300000 18880000
endmodule
